# Fritzing sketch Anemometer (saved by Fritzing 1.0.2b)
circuit board: 8.46667cm x 5.64444cm

parts:
  3-pins_Hall_Effect_Sensor = mystery part, 3 pins [chip_label="Hall Effect Sensor"]
  C1 = Tantalum Capacitor [capacitance=1μF voltage=35V package="200 mil [THT, tantalum]"]
  R1 = Resistor [tolerance=±5% power=0.25W resistance=1k package=THT]

nets:
  N1: 3-pins_Hall_Effect_Sensor.pin1, 3-pins_Hall_Effect_Sensor.pin3, C1.-, R1.Pin_0, R1.Pin_1
  N2: 3-pins_Hall_Effect_Sensor.pin2, C1.+

notes:
  Parts -
  - Honeywell SS451A bi-polar hall effects
  - Resistor (1000 Ohm)
  - Capacitor (0.01 Micro Farad)
  - M5 stack 20cm female dupont connector
  Use the dupont connectors (the ground, 3V, and SCL or SDA wires) to connect to the hall effects sensor. In this current configuration, the beveled side of the Honeywell sensor should be facing up, with the 3V wire (red) on the far right, the ground wire in the middle, and the SCL wire on the far right. The capicotor should be connected between the ground and 3V, and the resistor should be between the 3V and data wire (SDA, blue).
  This sensor is a digital analog sensor, and therefore senses binary signals over either the SCL or SDA wires. Whichever you choose, choose the opposite for the Anemometer Sensor.
  Use 1000 Ohm Resistor
  Anemometer
  This end is the M5 or Qwiic sensor plug in. The additional dupont (SDA wire, blue), can be removed from the sensor.
