# Fritzing sketch rain_gauge (saved by Fritzing 1.0.2b)

parts:
  C3 = Tantalum Capacitor [capacitance=1μF voltage=35V package="200 mil [THT, tantalum]"]
  R3 = Resistor [tolerance=±5% power=0.25W resistance=1k package=THT]
  3-pins_Hall_Effect_Sensor2 = mystery part, 3 pins [chip_label="Hall Effect Sensor"]

nets:
  N1: C3.-, R3.Pin_1, 3-pins_Hall_Effect_Sensor2.pin1
  N2: C3.+, 3-pins_Hall_Effect_Sensor2.pin2
  N3: R3.Pin_0, 3-pins_Hall_Effect_Sensor2.pin3

notes:
  Rain Gauge
  Parts -
  - Honeywell SS451A bi-polar hall effects
  - Resistor (1000 Ohm)
  - Capacitor (0.01 Micro Farad)
  - M5 stack 20cm female dupont connector
  Use the dupont connectors (the ground, 3V, and SLC or SDA wires) to connect to the hall effects sensor. In this current configuration, the beveled side of the Honeywell sensor should be facing up, with the 3V wire (red) on the far right, the ground wire in the middle, and the SDA wire on the far right. The capicotor should be connected between the ground and 3V, and the resistor should be between the 3V and data wire (SDA, blue).
  This sensor is a digital analog sensor, and therefore senses binary signals over either the SLC or SDA wires. Whichever you choose, choose the opposite for the Anemometer Sensor.
  This configuration is the same as the Anemometer, but uses the opposite data wire (if Anemometer uses SCL, then the rain gauge should use SDA).
  This end is the M5 or Qwiic sensor plug in. The additional dupont (SLC wire, yellow), can be removed from the sensor.
